// Logisim project 1_demi_additionneur.circ as structural Verilog: 1 circuit, main circuit main
module main (
  input  a0,
  input  b0,
  output out_3,
  output out_4
);

  xor xor_1 (out_3, a0, b0);
  and and_1 (out_4, a0, b0);
endmodule
