// Logisim project 4_horloge_numerique.circ as structural Verilog: 1 circuit, main circuit main
module main (
);

  wire and_1_out, clock_1_out, counter_2_carry, counter_3_carry, counter_4_carry, counter_5_carry,
       counter_6_carry;
  wire [3:0] counter_1_q, counter_2_q, counter_3_q, counter_4_q, counter_5_q, counter_6_q;

  and and_1 (and_1_out, counter_1_q[1], counter_2_q[2]);
  Hex_Digit_Display hex_digit_display_1 (.value(counter_1_q));  // open: dp
  Counter #(.width(4), .max('h5), .trigger("falling")) counter_1 (
    .Q(counter_1_q), .clk(counter_2_carry), .clr(and_1_out));  // open: load, D, count, carry
  Hex_Digit_Display hex_digit_display_2 (.value(counter_2_q));  // open: dp
  Counter #(.width(4), .max('h9), .trigger("falling")) counter_2 (
    .Q(counter_2_q), .carry(counter_2_carry), .clk(counter_3_carry), .clr(and_1_out));  // open: load, D, count
  Hex_Digit_Display hex_digit_display_3 (.value(counter_3_q));  // open: dp
  Counter #(.width(4), .max('h5), .trigger("falling")) counter_3 (
    .Q(counter_3_q), .carry(counter_3_carry), .clk(counter_4_carry));  // open: load, D, count, clr
  Hex_Digit_Display hex_digit_display_4 (.value(counter_4_q));  // open: dp
  Counter #(.width(4), .max('h9), .trigger("falling")) counter_4 (
    .Q(counter_4_q), .carry(counter_4_carry), .clk(counter_5_carry));  // open: load, D, count, clr
  Hex_Digit_Display hex_digit_display_5 (.value(counter_5_q));  // open: dp
  Counter #(.width(4), .max('h5), .trigger("falling")) counter_5 (
    .Q(counter_5_q), .carry(counter_5_carry), .clk(counter_6_carry));  // open: load, D, count, clr
  Clock clock_1 (.out(clock_1_out));
  Hex_Digit_Display hex_digit_display_6 (.value(counter_6_q));  // open: dp
  Counter #(.width(4), .max('h9)) counter_6 (
    .Q(counter_6_q), .carry(counter_6_carry), .clk(clock_1_out));  // open: load, D, count, clr

  // Notes on the sheet:
  //   4.Horloge numérique
  //   Heures
  //   Minutes
  //   Secondes
endmodule
