// Logisim project 5_controle_de_feux_de_circulation.circ as structural Verilog: 1 circuit, main circuit main
module main (
);

  wire _0_out, _1_out, _2_out, _3_out, button_1_out, not_1_out, not_2_out, not_3_out, not_4_out, or_1_out,
       or_2_out, or_3_out, or_4_out;
  wire [1:0] counter_1_q;

  Counter #(.width(2), .max('h3)) counter_1 (.Q(counter_1_q), .clk(button_1_out));  // open: load, D, count, carry, clr
  Button button_1 (.out(button_1_out));
  not not_1 (not_1_out, counter_1_q[0]);
  not not_2 (not_2_out, counter_1_q[1]);
  not not_3 (not_3_out, counter_1_q[1]);
  not not_4 (not_4_out, counter_1_q[0]);
  and _0 (_0_out, not_1_out, not_2_out);
  and _1 (_1_out, counter_1_q[0], not_3_out);
  and _2 (_2_out, not_4_out, counter_1_q[1]);
  and _3 (_3_out, counter_1_q[0], counter_1_q[1]);
  or or_1 (or_1_out, _3_out, _2_out);
  buf or_2 (or_2_out, _1_out);  // OR_Gate
  buf or_3 (or_3_out, _0_out);  // OR_Gate
  LED led_1 (.in(or_4_out));
  LED led_2 (.in(or_1_out));
  LED led_3 (.in(or_2_out));
  LED led_4 (.in(_3_out));
  LED led_5 (.in(or_3_out));
  LED led_6 (.in(_2_out));
  or or_4 (or_4_out, _0_out, _1_out);

  // Notes on the sheet:
  //   5. Contrôle de feux de circulation
  //   FEU1
  //   FEU2
endmodule
