// Logisim project 6_bonus_1.circ as structural Verilog: 2 circuits, main circuit main
module main (
);

  wire button_1_out;

  Counter #(.width(3), .max('h7)) counter_1 (.clk(button_1_out));  // open: load, D, count, Q, carry, clr
  Button button_1 (.out(button_1_out));
endmodule

module main2 (
);

  wire and_1_out, and_2_out, and_3_out, and_4_out, and_5_out, and_6_out, button_1_out, not_1_out, not_2_out,
       not_3_out, not_4_out, not_5_out, not_6_out, not_7_out, not_8_out, or_1_out, or_2_out;
  wire [2:0] counter_1_q;

  Button button_1 (.out(button_1_out));
  Counter #(.width(3), .max('h7)) counter_1 (.Q(counter_1_q), .clk(button_1_out));  // open: load, D, count, carry, clr
  not not_1 (not_1_out, counter_1_q[2]);
  not not_2 (not_2_out, counter_1_q[2]);
  not not_3 (not_3_out, counter_1_q[1]);
  not not_4 (not_4_out, counter_1_q[2]);
  not not_5 (not_5_out, counter_1_q[0]);
  not not_6 (not_6_out, counter_1_q[2]);
  and and_1 (and_1_out, counter_1_q[2], counter_1_q[1], counter_1_q[0]);
  not not_7 (not_7_out, counter_1_q[1]);
  not not_8 (not_8_out, counter_1_q[0]);
  and and_2 (and_2_out, not_1_out, counter_1_q[1], counter_1_q[0]);
  and and_3 (and_3_out, not_2_out, not_3_out);
  and and_4 (and_4_out, not_4_out, not_5_out);
  and and_5 (and_5_out, counter_1_q[2], not_7_out);
  and and_6 (and_6_out, counter_1_q[2], not_8_out);
  LED R1 (.in(counter_1_q[2]));
  LED O1 (.in(and_2_out));
  or or_1 (or_1_out, and_3_out, and_4_out);
  LED V1 (.in(or_1_out));
  LED R2 (.in(not_6_out));
  LED O2 (.in(and_1_out));
  LED V2 (.in(or_2_out));
  or or_2 (or_2_out, and_5_out, and_6_out);
endmodule
