// Logisim project 6_bonus_feux.circ as structural Verilog: 1 circuit, main circuit main
module main (
);

  wire button_1_out, decoder_1_out0, decoder_1_out1, decoder_1_out2, decoder_1_out3, or_1_out, or_2_out;
  wire [1:0] counter_1_q;

  Counter #(.width(2), .max('h3)) counter_1 (.Q(counter_1_q), .clk(button_1_out));  // open: load, D, count, carry, clr
  Button button_1 (.out(button_1_out));
  or or_1 (or_1_out, decoder_1_out3, decoder_1_out2);
  LED led_1 (.in(or_1_out));
  LED led_2 (.in(decoder_1_out1));
  LED led_3 (.in(decoder_1_out0));
  Decoder #(.select(2)) decoder_1 (
    .out0(decoder_1_out0), .out1(decoder_1_out1), .out2(decoder_1_out2), .out3(decoder_1_out3),
    .sel(counter_1_q));  // open: en
  or or_2 (or_2_out, decoder_1_out1, decoder_1_out0);
  LED led_4 (.in(or_2_out));
  LED led_5 (.in(decoder_1_out3));
  LED led_6 (.in(decoder_1_out2));

  // Notes on the sheet:
  //   5. Contrôle de feux de circulation
  //   FEU1
  //   FEU2
endmodule
