// Logisim project micro4.circ as structural Verilog
module Micro4 (
);

  wire and_1_out, and_2_out, and_3_out, and_4_out, and_5_out, and_6_out, and_7_out, c_alu_16_bits_1_negative,
       c_alu_16_bits_1_zero, c_cycle_1_etat_1, c_cycle_1_etat_2, c_cycle_1_etat_3, c_cycle_1_etat_4,
       clock_1_out, or_1_out;
  wire [3:0] ALU;
  wire [4:0] SAUTS;
  wire [15:0] A_q, B_q, c_alu_16_bits_1_output, c_compteur_16bits_1_output, c_mux_1_output, c_mux_2_output,
       C_q, register_1_q;
  wire [26:20] register_1_q_2;
  wire [31:0] rom_1_data;

  c_Cycle c_cycle_1 (
    .\Entrée_Horloge (clock_1_out), .Etat_1(c_cycle_1_etat_1), .Etat_2(c_cycle_1_etat_2),
    .Etat_3(c_cycle_1_etat_3), .Etat_4(c_cycle_1_etat_4));
  Clock clock_1 (.out(clock_1_out));
  c_Compteur_16bits c_compteur_16bits_1 (
    .Output(c_compteur_16bits_1_output), .Input(register_1_q), .Reset(or_1_out), .Control(c_cycle_1_etat_4));
  or or_1 (or_1_out, SAUTS[4], and_1_out, and_2_out, and_3_out, and_4_out);
  // Probe on c_compteur_16bits_1_output
  and and_1 (and_1_out, SAUTS[3], ~c_alu_16_bits_1_zero);  // AND_Gate
  and and_2 (and_2_out, SAUTS[2], c_alu_16_bits_1_zero);
  and and_3 (and_3_out, c_alu_16_bits_1_negative, SAUTS[1]);
  and and_4 (and_4_out, ~c_alu_16_bits_1_negative, SAUTS[0]);  // AND_Gate
  Register #(.width(32), .trigger("high")) register_1 (
    .D(rom_1_data), .Q({SAUTS, register_1_q_2, ALU, register_1_q}), .clk(c_cycle_1_etat_1));  // open: en, clr
  ROM #(.addrWidth(16), .dataWidth(32)) rom_1 (.addr(c_compteur_16bits_1_output), .data(rom_1_data));  // open: sel
  // Probe on {SAUTS, register_1_q_2, ALU}
  // Probe on register_1_q
  c_MUX c_mux_1 (.Output(c_mux_1_output), .Input_0(C_q), .Input_1(B_q), .Control(register_1_q_2[26]));
  and and_5 (and_5_out, c_cycle_1_etat_3, register_1_q_2[20]);
  // Probe on c_mux_2_output
  // Probe on c_mux_1_output
  c_ALU_16_bits c_alu_16_bits_1 (
    .Input_1(c_mux_1_output), .Input_0(c_mux_2_output), .Output(c_alu_16_bits_1_output),
    .Negative(c_alu_16_bits_1_negative), .Zero(c_alu_16_bits_1_zero), .C3(ALU[3]), .C2(ALU[2]), .C1(ALU[1]),
    .C0(ALU[0]), .Enable(c_cycle_1_etat_2));  // open: Carry
  // Probe on c_alu_16_bits_1_output
  Register #(.width(16)) C (.D(c_alu_16_bits_1_output), .Q(C_q), .clk(and_5_out));  // open: en, clr
  and and_6 (and_6_out, c_cycle_1_etat_3, register_1_q_2[21]);
  c_MUX c_mux_2 (.Output(c_mux_2_output), .Input_0(register_1_q), .Input_1(A_q), .Control(register_1_q_2[25]));
  Register #(.width(16)) B (.D(c_alu_16_bits_1_output), .Q(B_q), .clk(and_6_out));  // open: en, clr
  and and_7 (and_7_out, c_cycle_1_etat_3, register_1_q_2[22]);
  Register #(.width(16)) A (.D(c_alu_16_bits_1_output), .Q(A_q), .clk(and_7_out));  // open: en, clr
  Table_ALU table_alu_1 ();

  // Notes on the sheet:
  //   1.Lecture Mémoire
  //   4.Incrémentation Compteur
  //   Mémoire Programme
  //   JMP
  //   JMPNZ
  //   JMPZ
  //   JMPN
  //   JMPPZ
  //   2.Activation UAL
  //   Instruction
  //   3.Ecriture Registres
  //   Code opératoire
  //   DATA ou Adresse
  //   MUX1
  //   B
  //   C
  //   B
  //   C
  //   MUX0
  //   A
  //   B
  //   A
endmodule

module c_MUX (
  input  Control,
  input  [15:0] Input_0,
  input  [15:0] Input_1,
  output [15:0] Output
);

  Multiplexer #(.width(16), .enable("false")) multiplexer_1 (.in0(Input_0), .in1(Input_1), .out(Output), .sel(Control));
endmodule

module c_Cycle (
  input  \Entrée_Horloge ,
  output Etat_1,
  output Etat_2,
  output Etat_3,
  output Etat_4
);

  wire d_ff_1_q, d_ff_1_qn, d_ff_2_q, d_ff_2_qn, not_1_out;

  D_Flip_Flop d_ff_1 (.clk(\Entrée_Horloge ), .D(d_ff_1_qn), .Q(d_ff_1_q), .Qn(d_ff_1_qn));  // open: preset, en, reset
  not not_1 (not_1_out, \Entrée_Horloge );
  D_Flip_Flop d_ff_2 (.clk(not_1_out), .D(d_ff_2_qn), .Q(d_ff_2_q), .Qn(d_ff_2_qn));  // open: preset, en, reset
  and and_1 (Etat_1, ~d_ff_1_q, ~d_ff_2_q);  // AND_Gate
  and and_2 (Etat_2, d_ff_1_q, ~d_ff_2_q);  // AND_Gate
  and and_3 (Etat_3, d_ff_1_q, d_ff_2_q);
  and and_4 (Etat_4, ~d_ff_1_q, d_ff_2_q);  // AND_Gate
endmodule

module c_ALU_16_bits (
  input  [15:0] Input_1,
  input  [15:0] Input_0,
  input  C3,
  input  C2,
  input  C1,
  input  C0,
  input  Enable,
  output [15:0] Output,
  output Negative,
  output Zero,
  output Carry
);

  wire adder_1_cout, adder_2_cout, adder_3_cout, and_2_out, and_3_out, and_4_out, and_5_out, and_6_out,
       and_7_out, and_8_out, and_9_out, and_10_out, and_11_out, and_12_out, and_13_out, bitfinder_1_found,
       bitfinder_2_found, comparator_1_eq, comparator_1_lt, comparator_2_lt, decoder_1_out0, decoder_1_out3,
       decoder_1_out4, decoder_1_out5, decoder_1_out6, decoder_1_out7, decoder_1_out8, decoder_1_out9,
       decoder_1_out11, or_2_out, or_3_out, or_4_out, subtractor_1_bout, subtractor_2_bout, subtractor_3_bout;
  wire [15:0] adder_1_out, adder_2_out, adder_3_out, and_1_out, divider_1_out, multiplexer_1_out,
       multiplier_1_cout, multiplier_1_out, not_1_out, or_1_out, subtractor_1_out, subtractor_2_out,
       subtractor_3_out, xor_1_out;

  assign not_1_out = ~Input_0;  // NOT_Gate not_1, 16 bits wide
  assign and_1_out = Input_0 & Input_1;  // AND_Gate and_1, 16 bits wide
  assign or_1_out = Input_0 | Input_1;  // OR_Gate or_1, 16 bits wide
  Adder #(.width(16)) adder_1 (.a(Input_0), .b(16'h1), .out(adder_1_out), .cout(adder_1_cout));  // open: cin
  Subtractor #(.width(16)) subtractor_1 (
    .a(Input_0), .b(16'h1), .out(subtractor_1_out), .bout(subtractor_1_bout));  // open: bin
  Adder #(.width(16)) adder_2 (.a(Input_1), .b(16'h1), .out(adder_2_out), .cout(adder_2_cout));  // open: cin
  Subtractor #(.width(16)) subtractor_2 (
    .a(Input_1), .b(16'h1), .out(subtractor_2_out), .bout(subtractor_2_bout));  // open: bin
  Adder #(.width(16)) adder_3 (.a(Input_0), .b(Input_1), .out(adder_3_out), .cout(adder_3_cout));  // open: cin
  Subtractor #(.width(16)) subtractor_3 (
    .a(Input_0), .b(Input_1), .out(subtractor_3_out), .bout(subtractor_3_bout));  // open: bin
  Multiplier #(.width(16)) multiplier_1 (
    .a(Input_0), .b(Input_1), .out(multiplier_1_out), .cout(multiplier_1_cout));  // open: cin
  BitFinder #(.width(16)) bitfinder_1 (.in(multiplier_1_cout), .found(bitfinder_1_found));  // open: index
  Divider #(.width(16)) divider_1 (.a(Input_0), .b(Input_1), .out(divider_1_out));  // open: upper, rem
  Comparator #(.width(16)) comparator_1 (
    .a(Input_1), .b(Input_0), .eq(comparator_1_eq), .lt(comparator_1_lt));  // open: gt
  assign xor_1_out = Input_0 ^ Input_1;  // XOR_Gate xor_1, 16 bits wide
  Decoder #(.select(4)) decoder_1 (
    .out0(decoder_1_out0), .out3(decoder_1_out3), .out4(decoder_1_out4), .out5(decoder_1_out5),
    .out6(decoder_1_out6), .out7(decoder_1_out7), .out8(decoder_1_out8), .out9(decoder_1_out9),
    .out11(decoder_1_out11), .sel({C3, C2, C1, C0}));  // open: out1, out2, out10, out12, out13, out14, out15, en
  and and_2 (and_2_out, decoder_1_out11, comparator_1_lt);
  Multiplexer #(.select(4), .width(16)) multiplexer_1 (
    .in0({16{1'b0}}), .in1(Input_0), .in2(Input_1), .in3(adder_1_out), .in4(subtractor_1_out),
    .in5(adder_2_out), .in6(subtractor_2_out), .in7(adder_3_out), .in8(subtractor_3_out),
    .in9(multiplier_1_out), .in10(divider_1_out), .in11(Output), .in12(not_1_out), .in13(and_1_out),
    .in14(or_1_out), .in15(xor_1_out), .out(multiplexer_1_out), .sel({C3, C2, C1, C0}));  // open: en
  and and_3 (and_3_out, comparator_1_eq, decoder_1_out11);
  and and_4 (and_4_out, decoder_1_out9, bitfinder_1_found);
  and and_5 (and_5_out, decoder_1_out8, subtractor_3_bout);
  and and_6 (and_6_out, decoder_1_out7, adder_3_cout);
  and and_7 (and_7_out, decoder_1_out6, subtractor_2_bout);
  and and_8 (and_8_out, decoder_1_out5, adder_2_cout);
  and and_9 (and_9_out, decoder_1_out4, subtractor_1_bout);
  and and_10 (and_10_out, decoder_1_out3, adder_1_cout);
  // Probe on multiplexer_1_out
  Comparator #(.width(16)) comparator_2 (.a(multiplexer_1_out), .b({16{1'b0}}), .lt(comparator_2_lt));  // open: gt, eq
  BitFinder #(.width(16)) bitfinder_2 (.in(multiplexer_1_out), .found(bitfinder_2_found));  // open: index
  and and_11 (and_11_out, ~decoder_1_out0, Enable);  // AND_Gate
  and and_12 (and_12_out, comparator_2_lt, ~decoder_1_out11);  // AND_Gate
  and and_13 (and_13_out, ~bitfinder_2_found, ~decoder_1_out11);  // AND_Gate
  or or_2 (or_2_out, and_4_out, and_5_out, and_6_out, and_7_out, and_8_out, and_9_out, and_10_out);
  Register #(.width(16)) register_1 (.D(multiplexer_1_out), .Q(Output), .clk(and_11_out));  // open: en, clr
  or or_3 (or_3_out, and_2_out, and_12_out);
  or or_4 (or_4_out, and_13_out, and_3_out);
  Register #(.width(1)) register_2 (.D(or_3_out), .Q(Negative), .clk(and_11_out));  // open: en, clr
  Register #(.width(1)) register_3 (.D(or_4_out), .Q(Zero), .clk(and_11_out));  // open: en, clr
  Register #(.width(1)) register_4 (.D(or_2_out), .Q(Carry), .clk(and_11_out));  // open: en, clr

  // Notes on the sheet:
  //   0001 : I0
  //   0010 : I1
  //   0011 : I0+1
  //   0100 : I0-1
  //   0101 : I1+1
  //   0110 : I1-1
  //   0111 : I0+I1
  //   1000 : I0-I1
  //   1001 : I0*I1
  //   1010 : I0/I1
  //   1011 : I1 CMP I0
  //   1100 : NOT I0
  //   1101:I0 AND I1
  //   1110:I0 OR I1
  //   1111:I0 XOR I1
  //   1011 : NOT I0
  //   0000 : NOP
  //   1011 : I1 CMP I0
endmodule

module c_Compteur_16bits (
  input  [15:0] Input,
  input  Control,
  input  Reset,
  output [15:0] Output
);

  wire not_1_out;

  not not_1 (not_1_out, Reset);
  Counter #(.width(16), .max('hffff)) counter_1 (
    .load(Reset), .D(Input), .count(not_1_out), .Q(Output), .clk(Control));  // open: carry, clr
endmodule
